# Fritzing sketch CIRCUIT_DIAGRAM (saved by Fritzing 0.9.3b)
breadboards: 1

parts:
  74HC595_SHIFT_REGISTER = 74HC595 SMD [package="SO16 [SMD]"]
  7_SEGMENT_DISPLAY = 7 Segment Display
  R2 = Resistor [tolerance=±5% resistance=220 package=THT]
  MCU1 = ESP-WROOM-32 [ESP-32S] Module [part_number=ESP-WROOM-32]
  R3 = Resistor [tolerance=±5% resistance=220 package=THT]
  R5 = Resistor [tolerance=±5% resistance=220 package=THT]
  R6 = Resistor [tolerance=±5% resistance=220 package=THT]
  R7 = Resistor [tolerance=±5% resistance=220 package=THT]  # not connected
  R8 = Resistor [tolerance=±5% resistance=220 package=THT]
  R9 = Resistor [tolerance=±5% resistance=220 package=THT]
  R10 = Resistor [tolerance=±5% resistance=220 package=THT]
  IR_SENSOR1 = Infrared Proximity Sensor
  LDR = Photocell (LDR) [package=THT]
  RED_LED = smd LED [color="Red (633nm)" package="0603 [SMD]"]
  GREEN_LED = smd LED [color="Green (565nm)" package="0603 [SMD]"]
  YELLOW_LED = smd LED [color="Yellow (574nm)" package="0603 [SMD]"]
  SG90_SERVO_MOTOR3 = Basic Servo
  MT3608_BOOST_CONVERTER = MT3608 Boost No usb
  LM393_SOUND_SENSOR2 = Breakout Board for Electret Microphone
  LM2596_BUCK_CONVERTER = LM2596 [package=multiwatt15]
  SG90_SERVO_MOTOR1 = Basic Servo
  SG90_SERVO_MOTOR2 = Basic Servo
  SG90_SERVO_MOTOR4 = Basic Servo
  LDR1 = Photocell (LDR) [package=THT]
  R11 = Photocell (LDR) [package=THT]
  R12 = Photocell (LDR) [package=THT]
  IR_SENSOR2 = Infrared Proximity Sensor
  IR_SENSOR3 = Infrared Proximity Sensor
  IR_SENSOR4 = Infrared Proximity Sensor
  LM393_SOUND_SENSOR1 = Breakout Board for Electret Microphone
  LM393_SOUND_SENSOR4 = Breakout Board for Electret Microphone
  LM393_SOUND_SENSOR3 = Breakout Board for Electret Microphone
  C1 = Capacitor [package=cap-pth-5mm]
  HARDWARE_FILTER_CIRCUIT = Resistor [tolerance=±5% resistance=220 package=THT]  # not connected
  C2 = Capacitor [package=cap-pth-5mm]
  HARDWARE_FILTER_CIRCUIT1 = Resistor [tolerance=±5% resistance=220 package=THT]  # not connected
  C3 = Capacitor [package=cap-pth-5mm]
  HARDWARE_FILTER_CIRCUITS = Resistor [tolerance=±5% resistance=220 package=THT]
  C4 = Capacitor [package=cap-pth-5mm]
  HARDWARE_FILTER_CIRCUIT3 = Resistor [tolerance=±5% resistance=220 package=THT]
  HARDWARE_FILTER_CIRCUIT4 = Resistor [tolerance=±5% resistance=220 package=THT]
  HARDWARE_FILTER_CIRCUIT5 = Resistor [tolerance=±5% resistance=220 package=THT]
  HARDWARE_FILTER_CIRCUIT6 = Resistor [tolerance=±5% resistance=220 package=THT]
  1K = Resistor [tolerance=±5% resistance=220 package=THT]
  1K_2 = Resistor [tolerance=±5% resistance=220 package=THT]  # not connected
  1K_3 = Resistor [tolerance=±5% resistance=220 package=THT]
  1K_4 = Resistor [tolerance=±5% resistance=220 package=THT]
  C5 = Capacitor [package=cap-pth-5mm]
  C6 = Capacitor [package=cap-pth-5mm]
  C7 = Capacitor [package=cap-pth-5mm]
  C8 = Capacitor [package=cap-pth-5mm]
  BMS_GND = Header 1 [package=smtso-256-et]  # not connected
  BMS_Vin = Header 1 [package=smtso-256-et]

nets:
  N1: 74HC595_SHIFT_REGISTER.Q1, R10.Pin_1
  N2: 74HC595_SHIFT_REGISTER.Q2, R9.Pin_1
  N3: 74HC595_SHIFT_REGISTER.Q3, R8.Pin_1
  N4: 74HC595_SHIFT_REGISTER.Q5, R6.Pin_1
  N5: 74HC595_SHIFT_REGISTER.Q6, R5.Pin_1
  N6: 74HC595_SHIFT_REGISTER.Q7, R3.Pin_1
  GND: 74HC595_SHIFT_REGISTER.GND, 7_SEGMENT_DISPLAY.common_cathode, MCU1.Pin_1, MCU1.Pin_15, MCU1.Pin_38, IR_SENSOR1.GND, RED_LED.cathode, GREEN_LED.cathode, YELLOW_LED.cathode, MT3608_BOOST_CONVERTER.IN_(-), MT3608_BOOST_CONVERTER.OUT_(-), LM2596_BUCK_CONVERTER.GND, IR_SENSOR2.GND, IR_SENSOR3.GND, IR_SENSOR4.GND, HARDWARE_FILTER_CIRCUITS.Pin_1, C7.2, C8.1
  VCC: 74HC595_SHIFT_REGISTER.MR, 74HC595_SHIFT_REGISTER.VCC, MCU1.Pin_2, IR_SENSOR1.Vcc, LDR.pin_0, LM2596_BUCK_CONVERTER.Vout, LDR1.pin_0, R11.pin_0, R12.pin_1, IR_SENSOR2.Vcc, IR_SENSOR3.Vcc, IR_SENSOR4.Vcc, LM393_SOUND_SENSOR1.VCC, LM393_SOUND_SENSOR4.VCC, LM393_SOUND_SENSOR3.VCC, C5.1
  N7: 74HC595_SHIFT_REGISTER.SH_CP, MCU1.Pin_11
  N8: 74HC595_SHIFT_REGISTER.ST_CP, MCU1.Pin_10
  N9: 74HC595_SHIFT_REGISTER.DS, MCU1.Pin_8
  N10: 74HC595_SHIFT_REGISTER.Q0, R2.Pin_1
  N11: 7_SEGMENT_DISPLAY.Segment_A, R3.Pin_0
  N12: MCU1.Pin_13, HARDWARE_FILTER_CIRCUIT6.Pin_1
  N13: MCU1.Pin_14, HARDWARE_FILTER_CIRCUIT5.Pin_1
  N14: MCU1.Pin_16, HARDWARE_FILTER_CIRCUIT4.Pin_1
  N15: MCU1.Pin_18, C2.1
  N16: MCU1.Pin_19, C1.1
  N17: MCU1.Pin_20, C3.2
  N18: MCU1.Pin_21, C4.2
  N19: MCU1.Pin_22, IR_SENSOR1.Vout
  N20: MCU1.Pin_23, IR_SENSOR2.Vout
  N21: MCU1.Pin_24, IR_SENSOR3.Vout
  N22: MCU1.Pin_25, IR_SENSOR4.Vout
  N23: MCU1.Pin_26, R12.pin_0, 1K_4.Pin_0
  N24: MCU1.Pin_27, LDR1.pin_1, 1K_3.Pin_0
  N25: MCU1.Pin_29, LDR.pin_1
  N26: MCU1.Pin_30, R11.pin_1
  N27: MCU1.Pin_31, SG90_SERVO_MOTOR4.pulse
  N28: MCU1.Pin_33, SG90_SERVO_MOTOR3.pulse
  N29: MCU1.Pin_36, SG90_SERVO_MOTOR2.pulse
  N30: MCU1.Pin_37, SG90_SERVO_MOTOR1.pulse
  N31: RED_LED.anode, HARDWARE_FILTER_CIRCUIT4.Pin_0
  N32: GREEN_LED.anode, HARDWARE_FILTER_CIRCUIT5.Pin_0
  N33: YELLOW_LED.anode, HARDWARE_FILTER_CIRCUIT6.Pin_0
  GND_2: SG90_SERVO_MOTOR3.gnd, SG90_SERVO_MOTOR1.gnd, SG90_SERVO_MOTOR2.gnd, SG90_SERVO_MOTOR4.gnd
  VCC_2: SG90_SERVO_MOTOR3.vcc, MT3608_BOOST_CONVERTER.OUT_(+), SG90_SERVO_MOTOR1.vcc, SG90_SERVO_MOTOR2.vcc, SG90_SERVO_MOTOR4.vcc, C8.2
  N34: MT3608_BOOST_CONVERTER.IN_(+), C7.1
  GND_3: LM393_SOUND_SENSOR2.GND, LM393_SOUND_SENSOR1.GND, HARDWARE_FILTER_CIRCUIT3.Pin_1
  N35: LM2596_BUCK_CONVERTER.Vin, C6.2, BMS_Vin.1
  N36: LM393_SOUND_SENSOR1.AUD, C4.1
  N37: LM393_SOUND_SENSOR4.AUD, C1.2
  N38: LM393_SOUND_SENSOR3.AUD, C2.2
  N39: 1K.Pin_1, 1K_4.Pin_1

custom parts:
  ESP-WROOM-32 [ESP-32S] Module: Espressif ESP-WROOM-32 WiFi/Bluetooth LE microcontroller module also known as the Ai-Thinker ESP-32S module with similar formfactor. The ESP32 is a microcontroller chip with WiFi and BLE capabilities. The chip is developed by Espressif and is the successor to the popular ESP8266 WiFi module.
  MT3608 Boost No usb: Chip- MT3608 / B6289 DC to DC step up, power booster module. With adjustable output voltage. Current- 2A . || Input voltage- 2V-24V || Output voltage- 5V-28V Input interface- Inversed polarity- NO. || Led indicator- No.
  LM2596: LM2596 switching voltage regulator
